// Logisim project atividade_contadores.circ as structural Verilog: 1 circuit, main circuit main
module main (
);

  wire clock_1_out, FF0_q, FF0_qn, FF1_q, FF2_q, or_1_out;

  Clock clock_1 (.out(clock_1_out));
  or or_1 (or_1_out, FF0_qn, FF2_q);
  J_K_Flip_Flop FF2 (.J(FF0_qn), .K(FF0_qn), .clk(clock_1_out), .Q(FF2_q));  // open: Qn, preset, reset
  LED A2 (.in(FF2_q));
  J_K_Flip_Flop FF1 (.J(1'b1), .K(or_1_out), .clk(clock_1_out), .Q(FF1_q));  // open: Qn, preset, reset
  LED A1 (.in(FF1_q));
  J_K_Flip_Flop FF0 (.J(1'b1), .K(FF1_q), .clk(clock_1_out), .Q(FF0_q), .Qn(FF0_qn));  // open: preset, reset
  LED A0 (.in(FF0_q));

  // Notes on the sheet:
  //   Contador método sem especificação para 0, 1, 6
endmodule
