// Logisim project mini_computador.circ as structural Verilog
module comparador (
  input  A1,
  input  A0,
  input  B1,
  input  B0,
  output out_5
);

  wire not_1_out, not_2_out, xor_1_out, xor_2_out;

  xor xor_1 (xor_1_out, A1, B1);
  xor xor_2 (xor_2_out, A0, B0);
  not not_1 (not_1_out, xor_1_out);
  and and_1 (out_5, not_1_out, not_2_out);
  not not_2 (not_2_out, xor_2_out);

  // Notes on the sheet:
  //   Comparador de igualdade =
endmodule
