// Logisim project somador.circ as structural Verilog
module somador_literal (
  input  A,
  input  B,
  input  C,
  output S,
  output Cout
);

  wire and_1_out, and_2_out, and_3_out, and_4_out, and_5_out, and_6_out, and_7_out, and_8_out, and_9_out,
       and_10_out, not_1_out, not_2_out, not_3_out, not_4_out, not_5_out, not_6_out, not_7_out, or_1_out,
       or_2_out, or_3_out;

  not not_1 (not_1_out, A);
  not not_2 (not_2_out, B);
  not not_3 (not_3_out, A);
  not not_4 (not_4_out, B);
  not not_5 (not_5_out, B);
  and and_1 (and_1_out, not_5_out, C);
  and and_2 (and_2_out, B, not_6_out);
  not not_6 (not_6_out, C);
  and and_3 (and_3_out, B, C);
  and and_4 (and_4_out, A, B);
  and and_5 (and_5_out, not_1_out, not_2_out);
  and and_6 (and_6_out, not_3_out, B);
  and and_7 (and_7_out, A, not_4_out);
  or or_1 (or_1_out, and_1_out, and_2_out);
  or or_2 (or_2_out, and_4_out, and_5_out);
  not not_7 (not_7_out, C);
  or or_3 (or_3_out, and_6_out, and_7_out);
  and and_8 (and_8_out, A, or_1_out);
  and and_9 (and_9_out, C, or_2_out);
  and and_10 (and_10_out, not_7_out, or_3_out);
  or or_4 (Cout, and_8_out, and_3_out);
  or or_5 (S, and_9_out, and_10_out);
endmodule

module somador_quase_simplificado (
  input  A,
  input  B,
  input  C,
  output S,
  output Cout
);

  wire and_1_out, and_2_out, and_3_out, xor_1_out;

  and and_1 (and_1_out, A, B);
  and and_2 (and_2_out, A, C);
  and and_3 (and_3_out, B, C);
  or or_1 (Cout, and_1_out, and_2_out, and_3_out);
  xor xor_1 (xor_1_out, A, B);
  xor xor_2 (S, C, xor_1_out);
endmodule

module somador (
  input  A,
  input  B,
  input  C,
  output S,
  output Cout
);

  wire and_1_out, and_2_out, xor_1_out;

  and and_1 (and_1_out, A, B);
  xor xor_1 (xor_1_out, A, B);
  or or_1 (Cout, and_1_out, and_2_out);
  and and_2 (and_2_out, xor_1_out, C);
  xor xor_2 (S, C, xor_1_out);
endmodule
